# Fritzing sketch Schaltplan (saved by Fritzing 0.9.9b)
breadboards: 1

parts:
  Bauteil1 = Arduino Uno (Rev3)
  J1 = female pin header, 6 pins [form="♀ (female)"]
  J2 = female pin header, 6 pins [form="♀ (female)"]
  R1 = Resistor [tolerance=±5% power=0.25 resistance=10k package=THT]
  R2_(?) = Resistor [tolerance=±5% power=0.25 resistance=100k package=THT]
  R2_(?)1 = Resistor [tolerance=±5% power=0.25 resistance=100k package=THT]
  C1 = Ceramic Capacitor [capacitance=10pF voltage=35V package="100 mil [THT, multilayer]"]
  C2 = Ceramic Capacitor [capacitance=10pF voltage=35V package="100 mil [THT, multilayer]"]
  Bauteil2 = Arduino Uno (Rev3)
  S1 = Pushbutton [package="[THT]"]
  C3 = Ceramic Capacitor [capacitance=10pF voltage=35V package="100 mil [THT, multilayer]"]
  R2_(?)2 = Resistor [tolerance=±5% power=0.25 resistance=100k package=THT]
  S2 = Pushbutton [package="[THT]"]
  C4 = Ceramic Capacitor [capacitance=10pF voltage=35V package="100 mil [THT, multilayer]"]
  R2_(?)3 = Resistor [tolerance=±5% power=0.25 resistance=100k package=THT]
  R2 = Trimmer Potentiometer [maximum_resistance=100kΩ package=THT]
  R3 = Resistor [tolerance=±5% power=0.25 resistance=10k package=THT]

nets:
  N1: Bauteil1.A0, C2.1
  N2: Bauteil1.A1, J2.pin5, J2.pin6, R1.Pin_1
  N3: Bauteil1.A2, C1.1
  N4: Bauteil1.3V3, R2_(?).Pin_0, R2_(?)1.Pin_0
  N5: Bauteil1.5V, R1.Pin_0
  N6: Bauteil1.GND, J1.pin3, J2.pin2, J2.pin3
  N7: J1.pin4, J1.pin5, R2_(?)1.Pin_1, C1.0
  N8: J2.pin4, R2_(?).Pin_1, C2.0
  N9: Bauteil2.A0, C3.1
  N10: Bauteil2.A1, C4.1
  N11: Bauteil2.A2, R2.wiper, R3.Pin_1
  N12: Bauteil2.3V3, R2_(?)2.Pin_0, R2_(?)3.Pin_0
  N13: Bauteil2.5V, R3.Pin_0
  N14: Bauteil2.GND, S1.Pin_3, S1.Pin_4, S2.Pin_3, S2.Pin_4, R2.leg2
  N15: S1.Pin_1, S1.Pin_2, C3.0, R2_(?)2.Pin_1
  N16: S2.Pin_1, S2.Pin_2, C4.0, R2_(?)3.Pin_1

notes:
  Regenmesser
  Anemometer + Windfahne
  Regenmesser und Anenometer müssen sich eine Spannungsquelle teilen, da nur 2x VCC verfügbar
  => Problem (?), weil die Spannungsabnahme des einen Messgeräts die Spannung am analogen Input des anderen Geräts beeinflusst => verfälscht Messung, Trigger des einen Messgeräts, obwohl das andere ausschlägt
  Was macht der Kondensator vor dem analogen Input des Regenmessers? Braucht das Anemometer ebenfalls einen Kondensator?
  Anemometer
  Windfahne
